# Fritzing sketch Davay Ada-Feather1-RX (saved by Fritzing 0.9.4)
breadboards: 1

parts:
  Part1 = Adafruit Feather 32u4 RFM9xW LoRa [part_number="Adafruit #3078 and Adafruit #3079"]
  U1 = LIPO-1000mAh [package=lipo-1000]
  U2 = Chip antenna [package=antenna-chip3]
  LED2 = RGB LED (com. cathode, rgb) [package="5 mm [THT]"]
  S1 = Toggle Switch [package=THT]
  S2 = Toggle Switch [package=THT]
  S3 = Toggle Switch [package=THT]
  MOTOR1 = Vibration Motor
  S4 = Toggle Switch [package=THT]
  SG3 = Buzzer 12mm [package=buzzer-ccv-kit]
  LED1 = RGB LED (com. cathode, rgb) [package="5 mm [THT]"]
  Q1 = MOSFET-NCHANNEL [package=to-92]

nets:
  N1: Part1.ANT, U2.SIGNAL
  GND: Part1.GND, U1.-, S1.L1, MOTOR1.NEG, SG3.2, LED1.common_cathode
  N2: Part1.VBAT, U1.+, Q1.D
  N3: Part1.EN, S1.COM
  N4: Part1.6, Q1.G
  N5: LED2.red_anode, S3.L1
  N6: LED2.common_cathode, LED1.red_anode
  N7: S2.L1, SG3.1
  N8: S2.COM, S3.COM, S4.COM, Q1.S
  N9: MOTOR1.POS, S4.L1

custom parts:
  Adafruit Feather 32u4 RFM9xW LoRa: This is the Adafruit Feather 32u4 LoRa Radio (RFM9x) - our take on an microcontroller with a "Long Range (LoRa)" packet radio transceiver with built in USB and battery charging. Its an Adafruit Feather 32u4 with a 868/915 MHz radio module cooked in! Great for making wireless networks that can go further than 2.4GHz 802.15.4 and similar, are more flexible than Bluetooth LE and without the high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
  Vibration Motor: An eccentric vibration motor!
