# Fritzing sketch Davay Ada-Feather1 (saved by Fritzing 0.9.4)
breadboards: 1

parts:
  Part1 = Adafruit Feather 32u4 RFM9xW LoRa [part_number="Adafruit #3078 and Adafruit #3079"]
  U1 = LIPO-1000mAh [package=lipo-1000]
  U2 = Chip antenna [package=antenna-chip3]
  LED1 = RGB LED (com. cathode, rgb) [package="5 mm [THT]"]
  LED2 = RGB LED (com. cathode, rgb) [package="5 mm [THT]"]
  Q1 = NPN-Transistor [package="TO92 [THT]"]
  S1 = Toggle Switch [package=THT]
  LED3 = LED - 5mm [color="Red (633nm)" package="5 mm [THT]"]
  S2 = Toggle Switch [package=THT]
  S3 = Toggle Switch [package=THT]
  SG2 = Buzzer 12mm [package=buzzer-ccv-kit]
  MOTOR1 = Vibration Motor
  MOTOR2 = Vibration Motor
  S4 = Toggle Switch [package=THT]
  R1 = Resistor [tolerance=±5% resistance=3.3 power=0.25W package=THT]
  SG3 = Buzzer 12mm [package=buzzer-ccv-kit]

nets (from the schematic view):
  N1: Part1.ANT, U2.SIGNAL
  N2: Part1.GND, U1.-
  N3: Part1.VBAT, Q1.C, S1.L2
  N4: Part1.6, LED3.anode
  N5: Part1.5, Q1.B
  N6: U1.+, S1.COM
  N7: LED1.red_anode, LED2.red_anode, S3.L1
  N8: LED1.common_cathode, LED2.common_cathode, R1.Pin_0
  N9: Q1.E, S2.COM, S3.COM, S4.COM
  GND: LED3.cathode, SG2.2, MOTOR1.NEG, MOTOR2.NEG, R1.Pin_1, SG3.2
  N10: S2.L1, SG2.1, SG3.1
  N11: MOTOR1.POS, MOTOR2.POS, S4.L1

custom parts:
  Adafruit Feather 32u4 RFM9xW LoRa: This is the Adafruit Feather 32u4 LoRa Radio (RFM9x) - our take on an microcontroller with a "Long Range (LoRa)" packet radio transceiver with built in USB and battery charging. Its an Adafruit Feather 32u4 with a 868/915 MHz radio module cooked in! Great for making wireless networks that can go further than 2.4GHz 802.15.4 and similar, are more flexible than Bluetooth LE and without the high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
  Vibration Motor: An eccentric vibration motor!
