# Fritzing sketch TX-RX AdaFruit LoRa (saved by Fritzing 0.9.4)
breadboards: 2

parts:
  Part1 = Adafruit RFM9x LoRa Radio [part_number="Adafruit #3072 and #3073"]
  Part3 = Arduino Uno (Rev3) - ICSP
  ANT1 = Antenna
  S2 = Round Pushbutton
  LED4 = smd LED [color="Red (633nm)" package="0805 [SMD]"]
  R5 = Resistor [tolerance=±5% resistance=220 package="0805 [SMD]"]
  Part4 = Arduino Uno (Rev3) - ICSP
  Part5 = Adafruit RFM9x LoRa Radio [part_number="Adafruit #3072 and #3073"]
  ANT2 = Antenna
  LED5 = smd LED [color="Red (633nm)" package="0805 [SMD]"]
  R8 = Resistor [tolerance=±5% resistance=220 package="0805 [SMD]"]

nets:
  N1: Part1.ANTENNA, ANT1.antenna_lead
  5V: Part1.VIN, Part3.5V
  GND: Part1.GND, Part3.GND, S2.leg1, LED4.cathode
  N2: Part1.EN, Part3.D10_PWM/SS
  N3: Part1.DIO0, Part3.D2
  N4: Part1.SCK, Part3.D13/SCK
  N5: Part1.MISO, Part3.D12/MISO
  N6: Part1.MOSI, Part3.ICSP_MOSI, Part3.D11_PWM/MOSI
  N7: Part1.RST, Part3.D9_PWM
  N8: Part3.D5_PWM, R5.Pin_1
  N9: Part3.D6_PWM, S2.leg0
  N10: LED4.anode, R5.Pin_0
  N11: Part4.ICSP_MOSI, Part4.D11_PWM/MOSI, Part5.MOSI
  5V_2: Part4.5V, Part5.VIN
  GND_2: Part4.GND, Part5.GND, LED5.cathode
  N12: Part4.D9_PWM, Part5.RST
  N13: Part4.D10_PWM/SS, Part5.EN
  N14: Part4.D12/MISO, Part5.MISO
  N15: Part4.D13/SCK, Part5.SCK
  N16: Part4.D2, Part5.DIO0
  N17: Part4.D5_PWM, R8.Pin_1
  N18: Part5.ANTENNA, ANT2.antenna_lead
  N19: LED5.anode, R8.Pin_0

notes:
  433MHz = 16.5 cm
  PULLUP is used

custom parts:
  Adafruit RFM9x LoRa Radio: Sending data over long distances is like magic, and now you can be a magician with this range of powerful and easy-to-use radio modules. Sure, sometimes you want to talk to a computer (a good time to use WiFi) or perhaps communicate with a Phone (choose Bluetooth Low Energy!) but what if you want to send data very far? Most WiFi, Bluetooth, Zigbee and other wireless chipsets use 2.4GHz, which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
