# Fritzing sketch rfm69 (saved by Fritzing 0.9.3b)
breadboards: 1

parts:
  Part1 = Adafruit Metro with Headers [part_number="Adafruit #2488"]
  Part2 = Adafruit RFM69HCW Transceiver Radio [part_number="Adafruit #3070 and #3071"]

nets:
  GND: Part1.GND, Part2.GND
  N1: Part1.SCK, Part2.SCK
  N2: Part1.MISO, Part2.MISO
  N3: Part1.MOSI, Part2.MOSI
  N4: Part1.IO4, Part2.CS
  N5: Part1.IO3, Part2.DIO0
  N6: Part1.IO2, Part2.RST
  +5V: Part1.+5V, Part2.VIN

custom parts:
  Adafruit Metro with Headers: We sure love the ATmega328 here at Adafruit, and we use them a lot for our own projects. The processor has plenty of GPIO, Analog inputs, hardware UART SPI and I2C, timers and PWM galore - just enough for most simple projects. When we need to go small, we use a Pro Trinket 3V or 5V, but when size isn't as much of a concern, and an USB-serial converter is required, we reach for an Adafruit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
  Adafruit RFM69HCW Transceiver Radio: Sending data over long distances is like magic, and now you can be a magician with this range of powerful and easy-to-use radio modules. Sure, sometimes you want to talk to a computer (a good time to use WiFi) or perhaps communicate with a Phone (choose Bluetooth Low Energy!) but what if you want to send data very far? Most WiFi, Bluetooth, Zigbee and other wireless chipsets use 2.4GHz, which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
